// Logisim project lab3.circ as structural Verilog: 1 circuit, main circuit main
module main (
  input  in_1,
  input  in_2,
  input  J,
  input  C,
  input  K,
  output out_6,
  output out_7,
  output Q,
  output nQ
);

  wire nand_1_out, nand_2_out, nand_3_out, nand_4_out, nand_5_out, nand_6_out, nand_7_out, nand_8_out,
       nand_9_out, nand_10_out, nand_13_out, nand_14_out, undriven;

  nand nand_1 (nand_1_out, nQ, J, C);
  nand nand_2 (nand_2_out, C, K, Q);
  not nand_3 (nand_3_out, undriven);  // NAND_Gate
  nand nand_4 (nand_4_out, nand_3_out, undriven);
  nand nand_5 (nand_5_out, in_1, in_2);
  nand nand_6 (nand_6_out, nand_5_out, in_2);
  nand nand_7 (nand_7_out, nand_1_out, nand_8_out);
  nand nand_8 (nand_8_out, nand_7_out, nand_2_out);
  nand nand_9 (nand_9_out, nand_3_out, nand_10_out);
  nand nand_10 (nand_10_out, nand_9_out, nand_4_out);
  nand nand_11 (out_6, nand_5_out, out_7);
  nand nand_12 (out_7, out_6, nand_6_out);
  nand nand_13 (nand_13_out, nand_1_out, nand_7_out);
  nand nand_14 (nand_14_out, nand_8_out, nand_2_out);
  nand nand_15 (Q, nand_13_out, nQ);
  nand nand_16 (nQ, Q, nand_14_out);

  // Notes on the sheet:
  //   D-триггер
  //   T-триггер
  //   JK-триггер
endmodule
