// Logisim project lab6.circ as structural Verilog: 6 circuits, main circuit схема сравнения
module \схема_сравнения  (
  input  X1,
  input  X2,
  output Y
);

  wire and_1_out, and_2_out, not_1_out, not_2_out;

  not not_1 (not_1_out, X1);
  not not_2 (not_2_out, X2);
  and and_1 (and_1_out, not_1_out, X2);
  and and_2 (and_2_out, X1, not_2_out);
  or or_1 (Y, and_1_out, and_2_out);
endmodule

module \полусумматор  (
  input  in_1,
  input  in_2,
  output out_3,
  output out_4
);

  and and_1 (out_3, in_1, in_2);
  \схема_сравнения  \u_схема_сравнения  (.X1(in_1), .X2(in_2), .Y(out_4));

  // Notes on the sheet:
  //   полусумматор
endmodule

// SM
module \сумматор  (
  input  in_1,
  input  in_2,
  input  in_3,
  output out_4,
  output out_5
);

  wire \полусумматор_2_out_3 , \полусумматор_out_3 , \полусумматор_out_4 ;

  \полусумматор  \u_полусумматор  (
    .in_1(in_1), .in_2(in_2), .out_3(\полусумматор_out_3 ), .out_4(\полусумматор_out_4 ));
  \полусумматор  \u_полусумматор_2  (
    .in_1(\полусумматор_out_4 ), .in_2(in_3), .out_3(\полусумматор_2_out_3 ), .out_4(out_5));
  or or_1 (out_4, \полусумматор_out_3 , \полусумматор_2_out_3 );

  // Notes on the sheet:
  //   сумматор
endmodule

module \схема_из_4_сумматоров  (
  input  X4,
  input  Y4,
  input  X3,
  input  Y3,
  input  X2,
  input  Y2,
  input  X1,
  input  Y1,
  input  P0,
  output S5,
  output S4,
  output S3,
  output S2,
  output S1
);

  wire \сумматор_1_out_4 , \сумматор_2_out_4 , \сумматор_3_out_4 ;

  \сумматор  \u_сумматор_1  (.in_1(X1), .in_2(Y1), .in_3(P0), .out_4(\сумматор_1_out_4 ), .out_5(S1));
  \сумматор  \u_сумматор_2  (.in_1(X3), .in_2(Y3), .in_3(\сумматор_3_out_4 ), .out_4(\сумматор_2_out_4 ), .out_5(S3));
  \сумматор  \u_сумматор_3  (.in_1(X2), .in_2(Y2), .in_3(\сумматор_1_out_4 ), .out_4(\сумматор_3_out_4 ), .out_5(S2));
  \сумматор  \u_сумматор_4  (.in_1(X4), .in_2(Y4), .in_3(\сумматор_2_out_4 ), .out_4(S5), .out_5(S4));

  // Notes on the sheet:
  //   схемма 4 сумматоров
endmodule

module \теоретический_полусумматор  (
  input  in_1,
  input  in_2,
  output out_3,
  output out_4
);

  wire not_1_out, or_1_out;

  or or_1 (or_1_out, in_1, in_2);
  not not_1 (not_1_out, out_4);
  and and_1 (out_4, in_1, in_2);
  and and_2 (out_3, or_1_out, not_1_out);

  // Notes on the sheet:
  //   теоретический полусумматор
endmodule

module \теоретический_сумматор  (
  input  in_1,
  input  in_2,
  input  in_3,
  output out_4,
  output out_5
);

  wire and_1_out, and_2_out, and_3_out, and_4_out, and_5_out, not_1_out, or_1_out;

  and and_1 (and_1_out, in_1, in_2);
  and and_2 (and_2_out, in_1, in_3);
  and and_3 (and_3_out, in_2, in_2);
  or or_1 (or_1_out, in_1, in_2, in_2);
  and and_4 (and_4_out, in_1, in_2, in_2);
  or or_2 (out_4, and_1_out, and_2_out, and_3_out);
  not not_1 (not_1_out, out_4);
  and and_5 (and_5_out, not_1_out, or_1_out);
  or or_3 (out_5, and_5_out, and_4_out);

  // Notes on the sheet:
  //   теоретический сумматор
endmodule
